// Logisim project 4-way Traffic Light.circ as structural Verilog: 1 circuit, main circuit main
module main (
);

  wire A_out, and_1_out, and_2_out, and_3_out, and_4_out, and_5_out, and_6_out, and_7_out, and_8_out,
       and_9_out, and_10_out, and_11_out, and_12_out, B_out, C_out, D_out, not_1_out, not_2_out, not_3_out,
       not_4_out, not_5_out, not_6_out, not_7_out, not_8_out, not_9_out, not_10_out, not_11_out, not_12_out,
       or_1_out, or_2_out, or_3_out, or_4_out, or_5_out, or_6_out, or_7_out, or_8_out;

  Clock #(.highDuration(16), .lowDuration(16)) A (.out(A_out));
  Clock #(.highDuration(8), .lowDuration(8)) B (.out(B_out));
  Clock #(.highDuration(4), .lowDuration(4)) C (.out(C_out));
  Clock #(.highDuration(2), .lowDuration(2)) D (.out(D_out));
  not not_1 (not_1_out, A_out);
  not not_2 (not_2_out, B_out);
  not not_3 (not_3_out, C_out);
  not not_4 (not_4_out, D_out);
  or or_1 (or_1_out, A_out, B_out);
  and and_1 (and_1_out, not_1_out, not_2_out, C_out, D_out);
  and and_2 (and_2_out, not_2_out, not_1_out, not_3_out);
  and and_3 (and_3_out, not_2_out, not_1_out, not_4_out);
  or or_2 (or_2_out, and_2_out, and_3_out);
  or or_3 (or_3_out, A_out, not_2_out);
  and and_4 (and_4_out, C_out, B_out, D_out, not_1_out);
  and and_5 (and_5_out, B_out, not_1_out, not_3_out);
  and and_6 (and_6_out, B_out, not_1_out, not_4_out);
  or or_4 (or_4_out, and_5_out, and_6_out);
  LED led_1 (.in(or_3_out));
  LED led_2 (.in(and_4_out));
  LED led_3 (.in(or_4_out));
  LED led_4 (.in(or_1_out));
  LED led_5 (.in(and_1_out));
  LED led_6 (.in(or_2_out));
  not not_5 (not_5_out, A_out);
  not not_6 (not_6_out, B_out);
  not not_7 (not_7_out, C_out);
  not not_8 (not_8_out, D_out);
  not not_9 (not_9_out, A_out);
  not not_10 (not_10_out, B_out);
  not not_11 (not_11_out, C_out);
  not not_12 (not_12_out, D_out);
  and and_7 (and_7_out, A_out, B_out, C_out, D_out);
  and and_8 (and_8_out, A_out, not_6_out, C_out, D_out);
  and and_9 (and_9_out, A_out, not_6_out, not_7_out);
  and and_10 (and_10_out, A_out, not_6_out, not_8_out);
  or or_5 (or_5_out, not_9_out, not_10_out);
  and and_11 (and_11_out, not_11_out, A_out, B_out);
  and and_12 (and_12_out, A_out, B_out, not_12_out);
  or or_6 (or_6_out, not_5_out, B_out);
  or or_7 (or_7_out, and_9_out, and_10_out);
  or or_8 (or_8_out, and_11_out, and_12_out);
  LED led_7 (.in(or_6_out));
  LED led_8 (.in(and_8_out));
  LED led_9 (.in(or_7_out));
  LED led_10 (.in(or_5_out));
  LED led_11 (.in(and_7_out));
  LED led_12 (.in(or_8_out));
endmodule
