// Logisim project Simple Traffic light.circ as structural Verilog: 1 circuit, main circuit main
module main (
);

  wire clock_1_out, d_ff_1_q, d_ff_1_qn, nor_1_out, nor_2_out, nor_3_out, nor_4_out;

  Clock clock_1 (.out(clock_1_out));
  D_Flip_Flop d_ff_1 (
    .clk(clock_1_out), .D(d_ff_1_qn), .Q(d_ff_1_q), .Qn(d_ff_1_qn), .preset(1'b0), .en(1'b1), .reset(1'b0));
  nor nor_1 (nor_1_out, clock_1_out, d_ff_1_qn);
  nor nor_2 (nor_2_out, d_ff_1_q, d_ff_1_q);
  nor nor_3 (nor_3_out, clock_1_out, clock_1_out);
  LED led_1 (.in(d_ff_1_qn));
  LED led_2 (.in(nor_1_out));
  nor nor_4 (nor_4_out, nor_2_out, nor_3_out);
  LED led_3 (.in(nor_4_out));
endmodule
