// Logisim project Working one-way Traffic Light (FINAL).circ as structural Verilog: 1 circuit, main circuit main
module main (
);

  wire A_out, and_1_out, and_2_out, and_3_out, B_out, C_out, not_1_out, not_2_out, not_3_out, or_1_out;

  Clock #(.highDuration(8), .lowDuration(8)) A (.out(A_out));
  Clock #(.highDuration(4), .lowDuration(4)) B (.out(B_out));
  Clock #(.highDuration(2), .lowDuration(2)) C (.out(C_out));
  not not_1 (not_1_out, A_out);
  not not_2 (not_2_out, B_out);
  not not_3 (not_3_out, C_out);
  and and_1 (and_1_out, A_out, B_out, C_out);
  and and_2 (and_2_out, not_2_out, A_out);
  and and_3 (and_3_out, A_out, not_3_out);
  or or_1 (or_1_out, and_2_out, and_3_out);
  LED led_1 (.in(not_1_out));
  LED led_2 (.in(and_1_out));
  LED led_3 (.in(or_1_out));
endmodule
